// Logisim project 3 to 8 Decoder (AND).circ as structural Verilog: 1 circuit, main circuit main
module main (
  input  E,
  input  x2,
  input  x1,
  input  x0,
  output out_5,
  output out_6,
  output out_7,
  output out_8,
  output out_9,
  output out_10,
  output out_11,
  output out_12
);

  wire not_1_out, not_2_out, not_3_out;

  not not_1 (not_1_out, x2);
  not not_2 (not_2_out, x1);
  not not_3 (not_3_out, x0);
  and and_1 (out_5, not_1_out, not_2_out, not_3_out, E);
  and and_2 (out_6, not_1_out, not_2_out, x0, E);
  and and_3 (out_7, not_1_out, x1, not_3_out, E);
  and and_4 (out_8, not_1_out, x1, x0, E);
  and and_5 (out_9, x2, not_2_out, not_3_out, E);
  and and_6 (out_10, x2, not_2_out, x0, E);
  and and_7 (out_11, x2, x1, not_3_out, E);
  and and_8 (out_12, x2, x1, x0, E);

  // Notes on the sheet:
  //   d0
  //   d1
  //   d2
  //   d3
  //   d4
  //   d5
  //   d6
  //   d7
endmodule
