// Logisim project 3 to 8 Decoder (NAND).circ as structural Verilog: 1 circuit, main circuit main
module main (
  input  E,
  input  x2,
  input  x1,
  input  x0,
  output out_5,
  output out_6,
  output out_7,
  output out_8,
  output out_9,
  output out_10,
  output out_11,
  output out_12
);

  wire nand_1_out, nand_2_out, nand_3_out, nand_4_out, nand_5_out, nand_6_out, nand_7_out, nand_8_out,
       not_1_out, not_2_out, not_3_out;

  not not_1 (not_1_out, x2);
  not not_2 (not_2_out, x1);
  not not_3 (not_3_out, x0);
  nand nand_1 (nand_1_out, not_1_out, not_2_out, not_3_out, E);
  nand nand_2 (nand_2_out, not_1_out, not_2_out, x0, E);
  nand nand_3 (nand_3_out, not_1_out, x1, not_3_out, E);
  nand nand_4 (nand_4_out, not_1_out, x1, x0, E);
  nand nand_5 (nand_5_out, x2, not_2_out, not_3_out, E);
  nand nand_6 (nand_6_out, x2, not_2_out, x0, E);
  nand nand_7 (nand_7_out, x2, x1, not_3_out, E);
  nand nand_8 (nand_8_out, x2, x1, x0, E);
  nand nand_9 (out_5, nand_1_out, nand_1_out);
  nand nand_10 (out_6, nand_2_out, nand_2_out);
  nand nand_11 (out_7, nand_3_out, nand_3_out);
  nand nand_12 (out_8, nand_4_out, nand_4_out);
  nand nand_13 (out_9, nand_5_out, nand_5_out);
  nand nand_14 (out_10, nand_6_out, nand_6_out);
  nand nand_15 (out_11, nand_7_out, nand_7_out);
  nand nand_16 (out_12, nand_8_out, nand_8_out);

  // Notes on the sheet:
  //   d0
  //   d1
  //   d2
  //   d3
  //   d4
  //   d5
  //   d6
  //   d7
endmodule
