// Logisim project 4 bit Adder and Subtractor with MUX and FA (PDF 138 Rafiquzzaman).circ as structural Verilog: 1 circuit, main circuit main
module main (
  input  B3,
  input  A3,
  input  B2,
  input  A2,
  input  B1,
  input  A1,
  input  B0,
  input  A0,
  input  S,
  output C3,
  output S3,
  output S2,
  output S1,
  output S0
);

  wire main_2_out_5, main_3_out_5, main_4_out_5, multiplexer_1_out, multiplexer_2_out, multiplexer_3_out,
       multiplexer_4_out, not_1_out, not_2_out, not_3_out, not_4_out;

  Multiplexer multiplexer_1 (.in0(B3), .in1(not_1_out), .out(multiplexer_1_out), .sel(S));  // open: en
  not not_1 (not_1_out, B3);
  Full_Adder_3_input__User_Library__main main_1 (
    .A(main_2_out_5), .B(A3), .C_in(multiplexer_1_out), .out_4(S3), .out_5(C3));
  not not_2 (not_2_out, B2);
  Multiplexer multiplexer_2 (.in0(B2), .in1(not_2_out), .out(multiplexer_2_out), .sel(S));  // open: en
  Full_Adder_3_input__User_Library__main main_2 (
    .A(main_3_out_5), .B(A2), .C_in(multiplexer_2_out), .out_4(S2), .out_5(main_2_out_5));
  not not_3 (not_3_out, B1);
  Multiplexer multiplexer_3 (.in0(B1), .in1(not_3_out), .out(multiplexer_3_out), .sel(S));  // open: en
  Full_Adder_3_input__User_Library__main main_3 (
    .A(main_4_out_5), .B(A1), .C_in(multiplexer_3_out), .out_4(S1), .out_5(main_3_out_5));
  not not_4 (not_4_out, B0);
  Multiplexer multiplexer_4 (.in0(B0), .in1(not_4_out), .out(multiplexer_4_out), .sel(S));  // open: en
  Full_Adder_3_input__User_Library__main main_4 (
    .A(S), .B(A0), .C_in(multiplexer_4_out), .out_4(S0), .out_5(main_4_out_5));

  // Notes on the sheet:
  //   FA3
  //   C2
  //   FA2
  //   C1
  //   4-bit Adder/Subtractor with Multiplexer and Full Adder
  //   FA1
  //   C0
  //   FA0
endmodule
