// Logisim project 4 bit Adder and Subtractor.circ as structural Verilog: 1 circuit, main circuit main
module main (
  input  B3,
  input  A3,
  input  B2,
  input  A2,
  input  B1,
  input  A1,
  input  B0,
  input  A0,
  input  C,
  output C3,
  output S3,
  output S2,
  output S1,
  output S0
);

  wire main_2_out_5, main_3_out_5, main_4_out_5, xor_1_out, xor_2_out, xor_3_out, xor_4_out;

  xor xor_1 (xor_1_out, C, B3);
  Full_Adder_3_input__User_Library__main main_1 (.A(main_2_out_5), .B(A3), .C_in(xor_1_out), .out_4(S3), .out_5(C3));
  xor xor_2 (xor_2_out, C, B2);
  Full_Adder_3_input__User_Library__main main_2 (
    .A(main_3_out_5), .B(A2), .C_in(xor_2_out), .out_4(S2), .out_5(main_2_out_5));
  xor xor_3 (xor_3_out, C, B1);
  Full_Adder_3_input__User_Library__main main_3 (
    .A(main_4_out_5), .B(A1), .C_in(xor_3_out), .out_4(S1), .out_5(main_3_out_5));
  xor xor_4 (xor_4_out, C, B0);
  Full_Adder_3_input__User_Library__main main_4 (.A(C), .B(A0), .C_in(xor_4_out), .out_4(S0), .out_5(main_4_out_5));

  // Notes on the sheet:
  //   FA3
  //   C2
  //   FA2
  //   C1
  //   4-bit Adder/Subtractor
  //   FA1
  //   C0
  //   FA0
  //   Addition
  //   10 ---- 1 0 1 0
  //   (+) 3 ---- 0 0 1 1
  //   --------------------
  //   13 ---- 1 1 0 1
  //   C = 0, Adder
  //   C = 1, Subtractor
  //   Subtraction
  //   (+) 3 ---- 0 0 1 1
  //   1's com ---- 1 1 0 0
  //   (- 3) 2's com ---- 1 1 0 1
  //   10 ---- 1 0 1 0
  //   (+) (- 3) ---- 1 1 0 1
  //   --------------------
  //   7 -- 1 0 1 1 1
endmodule
