// Logisim project 4-16 Decoder using 2-4 Decoder.circ as structural Verilog: 1 circuit, main circuit main
module main (
  input  d0,
  input  d1,
  input  d2,
  input  d3,
  input  d4,
  input  d5,
  input  d6,
  input  E,
  input  d7,
  input  d8,
  input  [1:0] x3x2,
  input  d9,
  input  d10,
  input  [1:0] X1X0,
  input  d11,
  input  d12,
  input  d13,
  input  d14,
  input  d15
);

  wire decoder_1_out0, decoder_1_out1, decoder_1_out2, decoder_1_out3;

  Decoder #(.select(2)) decoder_1 (
    .out0(decoder_1_out0), .out1(decoder_1_out1), .out2(decoder_1_out2), .out3(decoder_1_out3), .sel(x3x2),
    .en(E));
  Decoder #(.select(2)) decoder_2 (.out0(d0), .out1(d1), .out2(d2), .out3(d3), .sel(X1X0), .en(decoder_1_out0));
  Decoder #(.select(2)) decoder_3 (.out0(d4), .out1(d5), .out2(d6), .out3(d7), .sel(X1X0), .en(decoder_1_out1));
  Decoder #(.select(2)) decoder_4 (.out0(d8), .out1(d9), .out2(d10), .out3(d11), .sel(X1X0), .en(decoder_1_out2));
  Decoder #(.select(2)) decoder_5 (.out0(d12), .out1(d13), .out2(d14), .out3(d15), .sel(X1X0), .en(decoder_1_out3));

  // Notes on the sheet:
  //   0
  //   1
  //   2
  //   3
  //   0
  //   1
  //   2
  //   3
  //   0
  //   1
  //   2
  //   3
  //   0
  //   1
  //   2
  //   3
endmodule
