// Logisim project Demultiplexer (1 to 8).circ as structural Verilog: 1 circuit, main circuit main
module main (
  input  E,
  input  i,
  input  S2,
  input  S1,
  input  S0,
  input  i_2,
  input  E_2,
  input  [2:0] S2S1S0
);

  wire and_1_out, and_2_out, and_3_out, and_4_out, and_5_out, and_6_out, and_7_out, and_8_out,
       demultiplexer_1_out0, demultiplexer_1_out1, demultiplexer_1_out2, demultiplexer_1_out3,
       demultiplexer_1_out4, demultiplexer_1_out5, demultiplexer_1_out6, demultiplexer_1_out7, not_1_out,
       not_2_out, not_3_out;

  Demultiplexer #(.select(3)) demultiplexer_1 (
    .out0(demultiplexer_1_out0), .out1(demultiplexer_1_out1), .out2(demultiplexer_1_out2),
    .out3(demultiplexer_1_out3), .out4(demultiplexer_1_out4), .out5(demultiplexer_1_out5),
    .out6(demultiplexer_1_out6), .out7(demultiplexer_1_out7), .in(i_2), .sel(S2S1S0), .en(E_2));
  not not_1 (not_1_out, S2);
  not not_2 (not_2_out, S1);
  not not_3 (not_3_out, S0);
  LED led_1 (.in(demultiplexer_1_out0));
  LED led_2 (.in(demultiplexer_1_out1));
  LED led_3 (.in(demultiplexer_1_out2));
  LED led_4 (.in(demultiplexer_1_out3));
  LED led_5 (.in(demultiplexer_1_out4));
  LED led_6 (.in(demultiplexer_1_out5));
  LED led_7 (.in(demultiplexer_1_out6));
  LED led_8 (.in(demultiplexer_1_out7));
  and and_1 (and_1_out, not_1_out, not_2_out, not_3_out, E, i);
  and and_2 (and_2_out, not_1_out, not_2_out, S0, E, i);
  and and_3 (and_3_out, not_1_out, S1, not_3_out, E, i);
  and and_4 (and_4_out, not_1_out, S1, S0, E, i);
  and and_5 (and_5_out, S2, not_2_out, not_3_out, E, i);
  and and_6 (and_6_out, S2, not_2_out, S0, E, i);
  and and_7 (and_7_out, S2, S1, not_3_out, E, i);
  and and_8 (and_8_out, S2, S1, S0, E, i);
  LED led_9 (.in(and_1_out));
  LED led_10 (.in(and_2_out));
  LED led_11 (.in(and_3_out));
  LED led_12 (.in(and_4_out));
  LED led_13 (.in(and_5_out));
  LED led_14 (.in(and_6_out));
  LED led_15 (.in(and_7_out));
  LED led_16 (.in(and_8_out));

  // Notes on the sheet:
  //   d0
  //   d1
  //   d2
  //   d3
  //   d4
  //   d5
  //   d6
  //   d7
  //   d2
  //   d3
  //   d4
  //   d5
  //   d6
  //   d7
  //   d0
  //   d1
endmodule
