// Logisim project Ex 2 with Decoder (PDF 136 Rafiquzzaman).circ as structural Verilog: 1 circuit, main circuit main
module main (
  input  E,
  input  x2,
  input  x1,
  input  x0,
  input  E_2,
  input  [2:0] x2x1x0,
  output out_7,
  output out_8,
  output out_9,
  output out_10,
  output out_11,
  output out_12,
  output out_13,
  output out_14
);

  wire decoder_1_out0, decoder_1_out1, decoder_1_out2, decoder_1_out3, decoder_1_out4, decoder_1_out5,
       decoder_1_out6, decoder_1_out7, not_1_out, not_2_out, not_3_out, or_1_out, or_2_out, or_3_out,
       or_4_out;

  not not_1 (not_1_out, x2);
  not not_2 (not_2_out, x1);
  not not_3 (not_3_out, x0);
  Decoder #(.select(3)) decoder_1 (
    .out0(decoder_1_out0), .out1(decoder_1_out1), .out2(decoder_1_out2), .out3(decoder_1_out3),
    .out4(decoder_1_out4), .out5(decoder_1_out5), .out6(decoder_1_out6), .out7(decoder_1_out7), .sel(x2x1x0),
    .en(E_2));
  and and_1 (out_7, not_1_out, not_2_out, not_3_out, E);
  and and_2 (out_8, not_1_out, not_2_out, x0, E);
  and and_3 (out_9, not_1_out, x1, not_3_out, E);
  and and_4 (out_10, not_1_out, x1, x0, E);
  and and_5 (out_11, x2, not_2_out, not_3_out, E);
  and and_6 (out_12, x2, not_2_out, x0, E);
  and and_7 (out_13, x2, x1, not_3_out, E);
  and and_8 (out_14, x2, x1, x0, E);
  or or_1 (or_1_out, decoder_1_out1, decoder_1_out2, decoder_1_out6, decoder_1_out7);
  or or_2 (or_2_out, decoder_1_out2, decoder_1_out3, decoder_1_out5, decoder_1_out6, decoder_1_out7);
  LED led_1 (.in(or_1_out));
  LED led_2 (.in(or_2_out));
  or or_3 (or_3_out, out_8, out_9, out_13, out_14);
  or or_4 (or_4_out, out_9, out_10, out_12, out_13, out_14);
  LED led_3 (.in(or_3_out));
  LED led_4 (.in(or_4_out));

  // Notes on the sheet:
  //   d0
  //   d1
  //   d2
  //   d3
  //   d4
  //   d5
  //   d6
  //   d7
  //   d0
  //   d1
  //   d2
  //   d3
  //   d4
  //   d5
  //   d6
  //   d7
  //   Z2
  //   Z1
  //   Z2
  //   Z1
endmodule
