// Logisim project Multiplexer (8 to 1).circ as structural Verilog: 1 circuit, main circuit main
module main (
  input  E,
  input  S2,
  input  S1,
  input  S0,
  input  d0,
  input  d1,
  input  d2,
  input  d3,
  input  d4,
  input  d5,
  input  d6,
  input  d7,
  input  d0_2,
  input  d1_2,
  input  d2_2,
  input  d3_2,
  input  d4_2,
  input  d5_2,
  input  d6_2,
  input  d7_2,
  input  [2:0] S2S1S0,
  input  E_2
);

  wire and_1_out, and_2_out, and_3_out, and_4_out, and_5_out, and_6_out, and_7_out, and_8_out,
       multiplexer_1_out, not_1_out, not_2_out, not_3_out, or_1_out;

  not not_1 (not_1_out, S2);
  not not_2 (not_2_out, S1);
  not not_3 (not_3_out, S0);
  Multiplexer #(.select(3)) multiplexer_1 (
    .in0(d0_2), .in1(d1_2), .in2(d2_2), .in3(d3_2), .in4(d4_2), .in5(d5_2), .in6(d6_2), .in7(d7_2),
    .out(multiplexer_1_out), .sel(S2S1S0), .en(E_2));
  LED led_1 (.in(multiplexer_1_out));
  and and_1 (and_1_out, not_1_out, not_2_out, not_3_out, d0, E);
  and and_2 (and_2_out, not_1_out, not_2_out, S0, d1, E);
  and and_3 (and_3_out, not_1_out, S1, not_3_out, d2, E);
  and and_4 (and_4_out, not_1_out, S1, S0, d3, E);
  and and_5 (and_5_out, S2, not_2_out, not_3_out, d4, E);
  and and_6 (and_6_out, S2, not_2_out, S0, d5, E);
  and and_7 (and_7_out, S2, S1, not_3_out, d6, E);
  and and_8 (and_8_out, S2, S1, S0, d7, E);
  or or_1 (or_1_out, and_1_out, and_2_out, and_3_out, and_4_out, and_5_out, and_6_out, and_7_out, and_8_out);
  LED led_2 (.in(or_1_out));

  // Notes on the sheet:
  //   Z
  //   d0
  //   d1
  //   d2
  //   d3
  //   d4
  //   d5
  //   d6
  //   d7
  //   Z
endmodule
