// Logisim project Shift Register (Incomplete).circ as structural Verilog: 1 circuit, main circuit main
module main (
  input  in_1,
  input  in_2,
  input  in_3,
  input  in_4,
  output out_5,
  output out_6,
  output out_7,
  output out_8
);

  wire and_1_out, and_2_out, and_3_out, and_4_out, and_5_out, and_6_out, and_7_out, and_8_out, or_1_out,
       or_2_out, or_3_out, or_4_out, undriven, undriven_2, undriven_3, undriven_4;

  Shift_Register shift_register_1 ();  // open: shift, in, clk, out, load, clr, d0, q0, d1, q1, d2, q2, d3, q3, d4, q4, d5, q5, d6, q6, d7, q7
  not not_1 (in_2, undriven_3);
  and and_1 (and_1_out, undriven, in_2);
  and and_2 (and_2_out, undriven_2, in_1);
  and and_3 (and_3_out, out_5, in_2);
  and and_4 (and_4_out, undriven_3, in_2);
  and and_5 (and_5_out, out_6, in_2);
  and and_6 (and_6_out, undriven_3, in_3);
  and and_7 (and_7_out, out_7, in_2);
  and and_8 (and_8_out, undriven_3, in_4);
  or or_1 (or_1_out, and_1_out, and_2_out);
  or or_2 (or_2_out, and_3_out, and_4_out);
  or or_3 (or_3_out, and_5_out, and_6_out);
  or or_4 (or_4_out, and_7_out, and_8_out);
  D_Flip_Flop d_ff_1 (.clk(undriven_4), .D(or_1_out), .Q(out_5));  // open: Qn, preset, en, reset
  D_Flip_Flop d_ff_2 (.clk(undriven_4), .D(or_2_out), .Q(out_6));  // open: Qn, preset, en, reset
  D_Flip_Flop d_ff_3 (.clk(undriven_4), .D(or_3_out), .Q(out_7));  // open: Qn, preset, en, reset
  D_Flip_Flop d_ff_4 (.clk(undriven_4), .D(or_4_out), .Q(out_8));  // open: Qn, preset, en, reset
  Clock clock_1 ();  // open: out
endmodule
